# Fritzing sketch clockin (saved by Fritzing 0.9.4)
circuit board: 8.46667cm x 5.64444cm

parts:
  U1 = NodeMCU V3.0
  M1 = pcf8574 io expansion board [package=THT]
  元件2 = RFID-RC522-v3
  S1 = Momentary Switch [package=ksa_sealed_tac_switch]
  S2 = Momentary Switch [package=ksa_sealed_tac_switch]
  S3 = Momentary Switch [package=ksa_sealed_tac_switch]
  Grove1 = Grove OLED 128x96
  J1 = Piezo Speaker
  part = NPN-Transistor [part_number=C1815 package="TO92 [THT]"]
  LED1 = smd LED [color="Blue (430nm)" package="1206 [SMD]"]
  二極體 = Diode [package=diode-1n4001]
  LED3 = smd LED [color="Blue (430nm)" package="1206 [SMD]"]
  LED4 = smd LED [color="Blue (430nm)" package="1206 [SMD]"]

nets:
  N1: U1.D0, 元件2.RST
  N2: U1.D1, M1.SCL, Grove1.SCL
  N3: U1.D2, M1.SDA
  N4: U1.D4, 元件2.SDA
  GND: U1.GND, M1.GND, 元件2.GND, S1.2, S2.2, S3.2, Grove1.GND, part.C
  N5: U1.D5, 元件2.SCK
  N6: U1.D6, 元件2.MISO
  N7: U1.D7, 元件2.MOSI
  VCC: U1.3V3, M1.VCC, 元件2.3.3V, Grove1.VCC
  N8: U1.Vin, 二極體.A
  N9: U1.S3, part.E
  N10: M1.O0, S3.3
  N11: M1.O1, S1.3
  N12: M1.O2, S2.3
  N13: J1.pin1, part.B, LED4.cathode
  N14: J1.pin2, LED1.anode, 二極體.C
  N15: LED1.cathode, LED3.anode
  N16: LED3.cathode, LED4.anode

custom parts:
  NodeMCU V3.0: ESP8266 based NodeMCU
  pcf8574 io expansion board: pcf8574 io expansion board.
  RFID-RC522-v3: A simple China made RFID-RC522 Reader (6x4 cm); do check the pin labels, as this is a MFRC522 based clone.
